// Logisim project 4-Bit-alu.circ as structural Verilog: 1 circuit, main circuit main
module main (
  input  F0,
  input  Enable_Input,
  input  A3,
  input  A2,
  input  F1,
  input  A1,
  input  A0,
  input  Enable_Input_2,
  input  B3,
  input  B2,
  input  B1,
  input  B0,
  input  F2,
  input  F3,
  input  F4
);

  wire A0_q, A1_q, A2_q, A3_q, adder_1_cout, adder_1_out, adder_2_cout, adder_2_out, adder_3_cout,
       adder_3_out, adder_4_cout, adder_4_out, and_1_out, and_2_out, and_3_out, and_4_out, and_5_out,
       and_6_out, and_7_out, and_8_out, and_9_out, and_10_out, and_11_out, and_12_out, and_13_out,
       and_14_out, and_15_out, and_16_out, and_17_out, and_18_out, and_19_out, and_20_out, and_21_out,
       and_22_out, and_23_out, and_24_out, and_25_out, and_26_out, and_27_out, and_28_out, and_29_out,
       and_30_out, and_31_out, and_32_out, and_33_out, B0_q, B1_q, B2_q, B3_q, Clear_2_out, Clear_out,
       Clock_out, not_1_out, not_2_out, not_3_out, or_1_out, or_2_out, or_3_out, or_4_out, or_5_out,
       or_6_out, or_7_out, or_8_out, or_9_out, or_10_out, or_11_out, or_12_out, or_13_out, or_14_out,
       or_15_out, or_16_out, or_17_out, xor_1_out, xor_2_out, xor_3_out, xor_4_out, xor_5_out, xor_6_out,
       xor_7_out, xor_8_out, xor_9_out, xor_10_out, xor_11_out, xor_12_out, xor_13_out, xor_14_out,
       xor_15_out, xor_16_out;

  Button Clock (.out(Clock_out));
  Button Clear (.out(Clear_out));
  Button Clear_2 (.out(Clear_2_out));
  D_Flip_Flop u_A3 (.clk(Clock_out), .D(A3), .Q(A3_q), .en(Enable_Input), .reset(Clear_out));  // open: Qn, preset
  D_Flip_Flop u_B3 (.clk(Clock_out), .D(B3), .Q(B3_q), .en(Enable_Input_2), .reset(Clear_2_out));  // open: Qn, preset
  D_Flip_Flop u_A2 (.clk(Clock_out), .D(A2), .Q(A2_q), .en(Enable_Input), .reset(Clear_out));  // open: Qn, preset
  D_Flip_Flop u_B2 (.clk(Clock_out), .D(B2), .Q(B2_q), .en(Enable_Input_2), .reset(Clear_2_out));  // open: Qn, preset
  D_Flip_Flop u_A1 (.clk(Clock_out), .D(A1), .Q(A1_q), .en(Enable_Input));  // open: Qn, preset, reset
  D_Flip_Flop u_B1 (.clk(Clock_out), .D(B1), .Q(B1_q), .en(Enable_Input_2));  // open: Qn, preset, reset
  xor xor_1 (xor_1_out, and_14_out, xor_9_out);
  xor xor_2 (xor_2_out, and_14_out, xor_10_out);
  xor xor_3 (xor_3_out, and_14_out, xor_11_out);
  xor xor_4 (xor_4_out, and_14_out, xor_12_out);
  D_Flip_Flop u_A0 (.clk(Clock_out), .D(A0), .Q(A0_q), .en(Enable_Input), .reset(Clear_out));  // open: Qn, preset
  D_Flip_Flop u_B0 (.clk(Clock_out), .D(B0), .Q(B0_q), .en(Enable_Input_2), .reset(Clear_2_out));  // open: Qn, preset
  Adder #(.width(1)) adder_1 (.a(xor_5_out), .b(xor_1_out), .out(adder_1_out), .cin(and_14_out), .cout(adder_1_cout));
  Adder #(.width(1)) adder_2 (.a(xor_6_out), .b(xor_2_out), .out(adder_2_out), .cin(adder_1_cout), .cout(adder_2_cout));
  Adder #(.width(1)) adder_3 (.a(xor_7_out), .b(xor_3_out), .out(adder_3_out), .cin(adder_2_cout), .cout(adder_3_cout));
  Adder #(.width(1)) adder_4 (.a(xor_8_out), .b(xor_4_out), .out(adder_4_out), .cin(adder_3_cout), .cout(adder_4_cout));
  not not_1 (not_1_out, F2);
  xor xor_5 (xor_5_out, F0, A3_q);
  xor xor_6 (xor_6_out, F0, A2_q);
  xor xor_7 (xor_7_out, F0, A1_q);
  xor xor_8 (xor_8_out, F0, A0_q);
  xor xor_9 (xor_9_out, F1, B3_q);
  xor xor_10 (xor_10_out, F1, B2_q);
  xor xor_11 (xor_11_out, F1, B1_q);
  xor xor_12 (xor_12_out, F1, B0_q);
  not not_2 (not_2_out, F3);
  not not_3 (not_3_out, F4);
  and and_1 (and_1_out, not_1_out, not_2_out);
  and and_2 (and_2_out, not_1_out, F3);
  and and_3 (and_3_out, F2, not_2_out);
  and and_4 (and_4_out, F2, F3);
  and and_5 (and_5_out, xor_5_out, xor_9_out);
  and and_6 (and_6_out, xor_6_out, xor_10_out);
  and and_7 (and_7_out, xor_7_out, xor_11_out);
  and and_8 (and_8_out, xor_8_out, xor_12_out);
  or or_1 (or_1_out, xor_5_out, xor_9_out);
  or or_2 (or_2_out, xor_6_out, xor_10_out);
  or or_3 (or_3_out, xor_7_out, xor_11_out);
  or or_4 (or_4_out, xor_8_out, xor_12_out);
  xor xor_13 (xor_13_out, xor_5_out, xor_9_out);
  xor xor_14 (xor_14_out, xor_6_out, xor_10_out);
  xor xor_15 (xor_15_out, xor_7_out, xor_11_out);
  xor xor_16 (xor_16_out, xor_8_out, xor_12_out);
  and and_9 (and_9_out, and_1_out, not_3_out);
  and and_10 (and_10_out, and_1_out, F4);
  and and_11 (and_11_out, and_2_out, not_3_out);
  and and_12 (and_12_out, and_2_out, F4);
  and and_13 (and_13_out, and_3_out, not_3_out);
  and and_14 (and_14_out, and_3_out, F4);
  and and_15 (and_15_out, and_4_out, not_3_out);
  and and_16 (and_16_out, and_4_out, F4);
  or or_5 (or_5_out, and_13_out, and_14_out);
  and and_17 (and_17_out, and_5_out, and_10_out);
  and and_18 (and_18_out, and_6_out, and_10_out);
  and and_19 (and_19_out, and_7_out, and_10_out);
  and and_20 (and_20_out, and_8_out, and_10_out);
  and and_21 (and_21_out, or_1_out, and_11_out);
  and and_22 (and_22_out, or_2_out, and_11_out);
  and and_23 (and_23_out, or_3_out, and_11_out);
  and and_24 (and_24_out, or_4_out, and_11_out);
  and and_25 (and_25_out, xor_13_out, and_12_out);
  and and_26 (and_26_out, xor_14_out, and_12_out);
  and and_27 (and_27_out, xor_15_out, and_12_out);
  and and_28 (and_28_out, xor_16_out, and_12_out);
  and and_29 (and_29_out, adder_4_out, or_5_out);
  and and_30 (and_30_out, adder_3_out, or_5_out);
  and and_31 (and_31_out, adder_2_out, or_5_out);
  and and_32 (and_32_out, adder_1_out, or_5_out);
  and and_33 (and_33_out, adder_4_cout, or_5_out);
  or or_6 (or_6_out, and_17_out, and_21_out);
  or or_7 (or_7_out, and_18_out, and_22_out);
  or or_8 (or_8_out, and_19_out, and_23_out);
  or or_9 (or_9_out, and_20_out, and_24_out);
  or or_10 (or_10_out, and_25_out, and_29_out);
  or or_11 (or_11_out, and_26_out, and_30_out);
  or or_12 (or_12_out, and_27_out, and_31_out);
  or or_13 (or_13_out, and_28_out, and_32_out);
  or or_14 (or_14_out, or_6_out, or_10_out);
  or or_15 (or_15_out, or_7_out, or_11_out);
  or or_16 (or_16_out, or_8_out, or_12_out);
  or or_17 (or_17_out, or_9_out, or_13_out);
  LED led_1 (.in(or_14_out));
  LED led_2 (.in(and_33_out));
  LED led_3 (.in(or_17_out));
  LED led_4 (.in(or_15_out));
  LED led_5 (.in(or_16_out));

  // Notes on the sheet:
  //   Subtract
  //   Registers
  //   Arithmetic Unit
  //   Logic Unit
  //   Decoder
  //   Cout
  //   Result
endmodule
